// Logisim project Project2Given.circ as structural Verilog: 4 circuits, main circuit main
module main (
);

  wire and_1_out, and_2_out, B0, B1, B2, B3, B4, B5, B6, B7, B8, B9, BL, BU, C0, C1, C2, CLK, L1_l, L1_u,
       not_1_out, or_8_out, P1_v, R0, R1, R3, R4, Valid;
  wire [2:0] counter_1_q;
  wire [3:0] IB1_c0, P1_b0, register_2_q, register_3_q, register_4_q, register_5_q;

  Button n1 (.out(B1));
  Button n4 (.out(B4));
  Button n7 (.out(B7));
  Button L (.out(BL));
  Button n3 (.out(B3));
  Button n2 (.out(B2));
  Button n6 (.out(B6));
  Button n5 (.out(B5));
  Button n9 (.out(B9));
  Button n8 (.out(B8));
  Button U (.out(BU));
  Button n0 (.out(B0));
  or or_1 (R0, B3, B2, B1);
  or or_2 (R1, B6, B5, B4);
  or or_3 (R3, B9, B8, B7);
  or or_4 (R4, BU, B0, BL);
  or or_5 (C0, B1, B4, B7, BL);
  or or_6 (C1, B2, B5, B8, B0);
  or or_7 (C2, B3, B6, B9, BU);
  Clock clock_1 (.out(CLK));
  nand nand_1 (Valid, IB1_c0[0], IB1_c0[1], IB1_c0[2], IB1_c0[3]);
  // Probe on P1_b0
  Panel P1 (
    .R0(R0), .R1(R1), .R2(R3), .R3(R4), .C0(C0), .C1(C1), .C2(C2), .B0(P1_b0[0]), .B1(P1_b0[1]),
    .B2(P1_b0[2]), .B3(P1_b0[3]), .V(P1_v));
  LED Press (.in(P1_v));
  // Probe on IB1_c0
  InputBuffer IB1 (
    .B0(P1_b0[0]), .B1(P1_b0[1]), .B2(P1_b0[2]), .B3(P1_b0[3]), .V(P1_v), .CLK(not_1_out), .C0(IB1_c0[0]),
    .C1(IB1_c0[1]), .C2(IB1_c0[2]), .C3(IB1_c0[3]));
  not not_1 (not_1_out, CLK);
  Register #(.width(4)) register_1 (.D(register_2_q), .en(Valid), .clk(CLK));  // open: Q, clr
  Lock L1 (.C0(IB1_c0[0]), .C1(IB1_c0[1]), .C2(IB1_c0[2]), .C3(IB1_c0[3]), .CLK(CLK), .L(L1_l), .U(L1_u));
  Counter #(.max('h7), .width(3)) counter_1 (
    .count(or_8_out), .Q(counter_1_q), .up(L1_u), .clk(CLK));  // open: load, D, carry, clr
  or or_8 (or_8_out, L1_l, L1_u);
  Register #(.width(4)) register_2 (.D(register_3_q), .en(Valid), .clk(CLK), .Q(register_2_q));  // open: clr
  LED Unlocked (.in(and_1_out));
  and and_1 (and_1_out, ~counter_1_q[0], ~counter_1_q[1], ~counter_1_q[2]);  // AND_Gate
  Register #(.width(4)) register_3 (.D(register_4_q), .en(Valid), .clk(CLK), .Q(register_3_q));  // open: clr
  LED Locked (.in(and_2_out));
  and and_2 (and_2_out, ~counter_1_q[0], ~counter_1_q[1], counter_1_q[2]);  // AND_Gate
  Register #(.width(4)) register_4 (.D(register_5_q), .en(Valid), .clk(CLK), .Q(register_4_q));  // open: clr
  Register #(.width(4)) register_5 (.D(IB1_c0), .en(Valid), .clk(CLK), .Q(register_5_q));  // open: clr
endmodule

module Panel (
  input  R0,
  input  R1,
  input  R2,
  input  R3,
  input  C0,
  input  C1,
  input  C2,
  output B0,
  output B1,
  output B2,
  output B3,
  output V
);

  wire and_1_out, and_2_out, and_3_out, and_4_out, and_5_out, and_6_out, and_7_out, and_8_out, and_9_out,
       and_10_out, and_12_out, and_13_out, and_14_out, and_15_out, and_16_out, and_17_out, and_18_out,
       and_19_out, CisEven, CisValid, nor_1_out, nor_2_out, nor_3_out, nor_4_out, nor_5_out, nor_6_out,
       nor_7_out, not_1_out, not_2_out, or_1_out, or_5_out, RisValid;

  nor nor_1 (nor_1_out, C1, C2);
  nor nor_2 (nor_2_out, C0, C2);
  nor nor_3 (nor_3_out, C1, C0);
  and and_1 (and_1_out, C0, nor_1_out);
  and and_2 (and_2_out, C1, nor_2_out);
  and and_3 (and_3_out, C2, nor_3_out);
  and and_4 (and_4_out, CisEven, or_1_out);
  or or_1 (or_1_out, R0, R2);
  and and_5 (and_5_out, R1, C1);
  and and_6 (and_6_out, C2, R3);
  or or_2 (CisValid, and_1_out, and_2_out, and_3_out);
  or or_3 (B0, and_4_out, and_5_out, and_6_out);
  and and_7 (and_7_out, R0, nor_4_out);
  nor nor_4 (nor_4_out, R1, R2, R3);
  and and_8 (and_8_out, R1, nor_5_out);
  nor nor_5 (nor_5_out, R0, R2, R3);
  and and_9 (and_9_out, R2, nor_6_out);
  nor nor_6 (nor_6_out, R1, R0, R3);
  and and_10 (and_10_out, R3, nor_7_out);
  nor nor_7 (nor_7_out, R1, R2, R0);
  and and_11 (V, RisValid, CisValid);
  or or_4 (RisValid, and_7_out, and_8_out, and_9_out, and_10_out);
  or or_5 (or_5_out, C1, C2);
  not not_1 (not_1_out, C1);
  not not_2 (not_2_out, C1);
  and and_12 (and_12_out, R0, or_5_out);
  and and_13 (and_13_out, R1, C2);
  and and_14 (and_14_out, R2, C0);
  and and_15 (and_15_out, R3, not_1_out);
  and and_16 (and_16_out, R3, not_2_out);
  and and_17 (and_17_out, R2, C1);
  and and_18 (and_18_out, R2, C2);
  or or_6 (B2, R1, and_19_out);
  and and_19 (and_19_out, R2, C0);
  or or_7 (B3, and_16_out, and_17_out, and_18_out);
  or or_8 (B1, and_12_out, and_13_out, and_14_out, and_15_out);
  or or_9 (CisEven, C0, C2);
endmodule

module InputBuffer (
  input  B0,
  input  B1,
  input  B2,
  input  B3,
  input  V,
  input  CLK,
  output C0,
  output C1,
  output C2,
  output C3
);

  wire and_1_out, and_2_out, and_4_out, and_5_out, B0out, B1out, B2out, B3out, d_ff_1_q, d_ff_1_qn,
       d_ff_2_qn, NoCode, not_1_out, not_2_out, not_3_out, not_4_out, or_1_out, SetNumber;

  and and_1 (and_1_out, d_ff_1_q, V);
  and and_2 (and_2_out, V, SetNumber);
  and and_3 (NoCode, C0, C1, C2, C3);
  and and_4 (and_4_out, V, and_5_out);
  D_Flip_Flop d_ff_1 (.D(or_1_out), .clk(CLK), .Q(d_ff_1_q), .Qn(d_ff_1_qn));  // open: preset, reset
  or or_1 (or_1_out, and_1_out, and_2_out);
  D_Flip_Flop d_ff_2 (.D(and_4_out), .clk(CLK), .Q(SetNumber), .Qn(d_ff_2_qn));  // open: preset, reset
  Register #(.width(1)) register_1 (.D(B0), .en(NoCode), .clk(CLK), .Q(B0out));  // open: clr
  and and_5 (and_5_out, d_ff_1_qn, d_ff_2_qn);
  Register #(.width(1)) register_2 (.D(B1), .en(NoCode), .clk(CLK), .Q(B1out));  // open: clr
  not not_1 (not_1_out, SetNumber);
  or or_2 (C0, not_1_out, B0out);
  not not_2 (not_2_out, SetNumber);
  or or_3 (C1, not_2_out, B1out);
  Register #(.width(1)) register_3 (.D(B2), .en(NoCode), .clk(CLK), .Q(B2out));  // open: clr
  not not_3 (not_3_out, SetNumber);
  not not_4 (not_4_out, SetNumber);
  Register #(.width(1)) register_4 (.D(B3), .en(NoCode), .clk(CLK), .Q(B3out));  // open: clr
  or or_4 (C2, not_3_out, B2out);
  or or_5 (C3, not_4_out, B3out);
endmodule

module Lock (
  input  C0,
  input  C1,
  input  C2,
  input  C3,
  input  CLK,
  output L,
  output U
);

  wire D1, D2, D3, Digit, I0, I1, I2, I3, I_isDigit, ILC, Invalid, IsL, IsU, IUC, J0, J1, J2, J3, J_isDigit,
       JLC, JUC, K0, K1, K2, K3, K_isDigit, KLC, KUC, LatestIsL, LC, LKMCS_one, Locked, MCS, MotorDone,
       multiplexer_1_out, multiplexer_2_out, not_1_out, not_2_out, not_3_out, not_4_out, not_5_out,
       not_6_out, not_7_out, not_8_out, not_9_out, not_10_out, not_11_out, not_12_out, not_13_out,
       not_14_out, not_15_out, not_16_out, not_17_out, not_18_out, not_19_out, not_20_out, not_21_out,
       not_22_out, not_23_out, not_24_out, not_25_out, not_26_out, not_27_out, not_28_out, not_29_out,
       not_30_out, not_31_out, not_32_out, not_33_out, not_34_out, not_35_out, not_36_out, not_37_out,
       or_1_out, SecondLatestIsL, SetCode, UC, ULMCS, Unlocked, xnor_1_out, xnor_2_out, xnor_3_out,
       xnor_4_out, xnor_5_out, xnor_6_out, xnor_7_out, xnor_8_out, xnor_9_out, xnor_10_out, xnor_11_out,
       xnor_12_out, xor_1_out, Y0, Y1;
  wire [1:0] counter_1_q;
  wire [3:0] register_1_q, register_4_q, register_6_q, register_7_q;

  not not_1 (not_1_out, Y0);
  xor xor_1 (xor_1_out, Y1, Y0);
  Multiplexer multiplexer_1 (.in0(Y1), .in1(xor_1_out), .out(multiplexer_1_out), .sel(MCS));
  Multiplexer multiplexer_2 (.in0(Y0), .in1(not_1_out), .out(multiplexer_2_out), .sel(MCS));
  Register #(.width(4)) register_1 (.D({I3, I2, I1, I0}), .en(SetCode), .clk(CLK), .Q(register_1_q));  // open: clr
  D_Flip_Flop d_ff_1 (.D(multiplexer_1_out), .clk(CLK), .Q(Y1));  // open: Qn, preset, reset
  D_Flip_Flop d_ff_2 (.D(multiplexer_2_out), .clk(CLK), .Q(Y0));  // open: Qn, preset, reset
  Counter #(.max('h3), .width(2)) counter_1 (.count(Y0), .Q(counter_1_q), .clk(CLK));  // open: load, D, carry, up, clr
  Register #(.width(4)) register_2 (
    .D({C3, C2, C1, C0}), .en(not_2_out), .clk(CLK), .Q({I3, I2, I1, I0}));  // open: clr
  not not_2 (not_2_out, Invalid);
  not not_3 (not_3_out, I1);
  not not_4 (not_4_out, I3);
  not not_5 (not_5_out, I1);
  and and_1 (Locked, Y1, not_6_out);
  not not_6 (not_6_out, Y0);
  and and_2 (MotorDone, counter_1_q[0], counter_1_q[1]);
  not not_7 (not_7_out, I0);
  not not_8 (not_8_out, I2);
  and and_3 (ILC, I0, not_3_out, I2, not_4_out);
  and and_4 (IUC, I0, not_5_out, I2, I3);
  not not_9 (not_9_out, Y1);
  xnor xnor_1 (xnor_1_out, I0, register_1_q[0]);
  xnor xnor_2 (xnor_2_out, I1, register_1_q[1]);
  xnor xnor_3 (xnor_3_out, I2, register_1_q[2]);
  xnor xnor_4 (xnor_4_out, I3, register_1_q[3]);
  and and_5 (LatestIsL, not_7_out, I1, not_8_out, I3);
  not not_10 (not_10_out, Y1);
  not not_11 (not_11_out, Y0);
  and and_6 (L, MotorDone, Y1);
  and and_7 (U, MotorDone, not_9_out);
  and and_8 (D3, xnor_1_out, xnor_2_out, xnor_3_out, xnor_4_out);
  and and_9 (ULMCS, IsU, D1, Locked, D2, D3);
  not not_12 (not_12_out, ILC);
  and and_10 (I_isDigit, not_12_out, not_13_out);
  not not_13 (not_13_out, IUC);
  not not_14 (not_14_out, C1);
  not not_15 (not_15_out, C3);
  not not_16 (not_16_out, C1);
  and and_11 (Unlocked, not_10_out, not_11_out);
  Register #(.width(4)) register_3 (
    .D({I3, I2, I1, I0}), .en(not_17_out), .clk(CLK), .Q({J3, J2, J1, J0}));  // open: clr
  not not_17 (not_17_out, Invalid);
  Register #(.width(4)) register_4 (.D({J3, J2, J1, J0}), .en(SetCode), .clk(CLK), .Q(register_4_q));  // open: clr
  nor nor_1 (Digit, Invalid, LC, UC);
  and and_12 (LC, C0, not_14_out, C2, not_15_out);
  and and_13 (UC, C0, not_16_out, C2, C3);
  and and_14 (Invalid, C0, C1, C2, C3);
  not not_18 (not_18_out, J1);
  not not_19 (not_19_out, J3);
  not not_20 (not_20_out, J1);
  and and_15 (LKMCS_one, Unlocked, LatestIsL, SecondLatestIsL);
  xnor xnor_5 (xnor_5_out, J0, register_4_q[0]);
  xnor xnor_6 (xnor_6_out, J1, register_4_q[1]);
  xnor xnor_7 (xnor_7_out, J2, register_4_q[2]);
  xnor xnor_8 (xnor_8_out, J3, register_4_q[3]);
  not not_21 (not_21_out, J0);
  and and_16 (SecondLatestIsL, not_21_out, J1, not_22_out, J3);
  not not_22 (not_22_out, J2);
  and and_17 (JLC, J0, not_18_out, J2, not_19_out);
  and and_18 (JUC, J0, not_20_out, J2, J3);
  and and_19 (SetCode, IsL, I_isDigit, J_isDigit, K_isDigit, Unlocked);
  and and_20 (D2, xnor_5_out, xnor_6_out, xnor_7_out, xnor_8_out);
  not not_23 (not_23_out, JLC);
  not not_24 (not_24_out, JUC);
  and and_21 (J_isDigit, not_23_out, not_24_out);
  Register #(.width(4)) register_5 (
    .D({J3, J2, J1, J0}), .en(not_25_out), .clk(CLK), .Q({K3, K2, K1, K0}));  // open: clr
  not not_25 (not_25_out, Invalid);
  Register #(.width(4)) register_6 (.D({K3, K2, K1, K0}), .en(SetCode), .clk(CLK), .Q(register_6_q));  // open: clr
  not not_26 (not_26_out, K1);
  not not_27 (not_27_out, K3);
  not not_28 (not_28_out, K1);
  or or_1 (or_1_out, LKMCS_one, MotorDone, SetCode, ULMCS);
  not not_29 (not_29_out, MotorDone);
  not not_30 (not_30_out, Y0);
  not not_31 (not_31_out, MotorDone);
  // OR_Gate or_2 has open pins: in0=not_29_out, in1=not_30_out, out=open
  xnor xnor_9 (xnor_9_out, K0, register_6_q[0]);
  xnor xnor_10 (xnor_10_out, K1, register_6_q[1]);
  xnor xnor_11 (xnor_11_out, K2, register_6_q[2]);
  xnor xnor_12 (xnor_12_out, K3, register_6_q[3]);
  and and_22 (KLC, K0, not_26_out, K2, not_27_out);
  and and_23 (KUC, K0, not_28_out, K2, K3);
  and and_24 (MCS, or_1_out, not_31_out);
  Register #(.width(4)) register_7 (.D({K3, K2, K1, K0}), .en(not_32_out), .clk(CLK), .Q(register_7_q));  // open: clr
  not not_32 (not_32_out, Invalid);
  and and_25 (D3, xnor_9_out, xnor_10_out, xnor_11_out, xnor_12_out);
  not not_33 (not_33_out, KLC);
  not not_34 (not_34_out, KUC);
  and and_26 (K_isDigit, not_33_out, not_34_out);
  not not_35 (not_35_out, register_7_q[1]);
  not not_36 (not_36_out, register_7_q[1]);
  not not_37 (not_37_out, register_7_q[3]);
  and and_27 (IsU, register_7_q[0], not_35_out, register_7_q[2], register_7_q[3]);
  and and_28 (IsL, register_7_q[0], not_36_out, register_7_q[2], not_37_out);
endmodule
